// Logisim project RISCVlib.circ as structural Verilog: 13 circuits, main circuit Register file
module InstDecoder (
  input  [31:0] IB,
  output [6:0] IB6_0,
  output [4:0] IB11_7,
  output [2:0] IB14_12,
  output [4:0] IB19_15,
  output [4:0] IB24_20,
  output [6:0] IB31_25
);


  assign IB6_0 = IB[6:0];
  assign IB11_7 = IB[11:7];
  assign IB14_12 = IB[14:12];
  assign IB19_15 = IB[19:15];
  assign IB24_20 = IB[24:20];
  assign IB31_25 = IB[31:25];
endmodule

module Extender (
  input  [31:0] IB,
  input  [2:0] TYPE,
  output [31:0] OUT
);

  wire [31:0] bit_extender_1_out, bit_extender_2_out, bit_extender_3_out, bit_extender_4_out,
       multiplexer_1_out;

  assign bit_extender_1_out = {{20{IB[31]}}, IB[31:20]};  // Bit_Extender bit_extender_1
  assign bit_extender_2_out = {{20{IB[31]}}, {IB[31:25], IB[11:7]}};  // Bit_Extender bit_extender_2
  assign bit_extender_3_out = {{19{IB[31]}}, {IB[31], IB[7], IB[30:25], IB[11:8], 1'b0}};  // Bit_Extender bit_extender_3
  assign bit_extender_4_out = {{11{IB[31]}}, {IB[31], IB[19:12], IB[20], IB[30:21], 1'b0}};  // Bit_Extender bit_extender_4
  Multiplexer #(.select(2), .width(32), .enable("false")) multiplexer_1 (
    .in0(bit_extender_1_out), .in1(bit_extender_2_out), .in2(bit_extender_3_out),
    .in3({IB[31:12], {12{1'b0}}}), .out(multiplexer_1_out), .sel(TYPE[1:0]));
  Multiplexer #(.width(32), .enable("false")) multiplexer_2 (
    .in0(multiplexer_1_out), .in1(bit_extender_4_out), .out(OUT), .sel(TYPE[2]));

  // Notes on the sheet:
  //   tipo-I
  //   tipo-S
  //   tipo-B
  //   tipo-U
  //   tipo-J
  //   TYPE    OUT
  //    000    extensión tipo-I
  //    001    extensión tipo-S
  //    010    extensión tipo-B
  //    011    extensión tipo-U
  //   100    extensión tipo-J
endmodule

module Register_file (
  input  clk,
  input  [4:0] Read_Register_1,
  input  [4:0] Read_Register_2,
  input  [4:0] Write_Register,
  input  [31:0] Write_Data,
  input  Write,
  output [31:0] Read_Data_1,
  output [31:0] Read_Data_2
);

  wire decoder_1_out1, decoder_1_out2, decoder_1_out3, decoder_1_out4, decoder_1_out5, decoder_1_out6,
       decoder_1_out7, decoder_1_out8, decoder_1_out9, decoder_1_out10, decoder_1_out11, decoder_1_out12,
       decoder_1_out13, decoder_1_out14, decoder_1_out15, decoder_1_out16, decoder_1_out17, decoder_1_out18,
       decoder_1_out19, decoder_1_out20, decoder_1_out21, decoder_1_out22, decoder_1_out23, decoder_1_out24,
       decoder_1_out25, decoder_1_out26, decoder_1_out27, decoder_1_out28, decoder_1_out29, decoder_1_out30,
       decoder_1_out31;
  wire [31:0] delayer1x32_1_out, multiplexer_1_out, multiplexer_2_out, R1_q, R2_q, R3_q, R4_q, R5_q, R6_q,
       R7_q, R8_q, R9_q, R10_q, R11_q, R12_q, R13_q, R14_q, R15_q, R16_q, R17_q, R18_q, R19_q, R20_q, R21_q,
       R22_q, R23_q, R24_q, R25_q, R26_q, R27_q, R28_q, R29_q, R30_q, R31_q;

  Decoder #(.select(5), .disabled(0)) decoder_1 (
    .out1(decoder_1_out1), .out2(decoder_1_out2), .out3(decoder_1_out3), .out4(decoder_1_out4),
    .out5(decoder_1_out5), .out6(decoder_1_out6), .out7(decoder_1_out7), .out8(decoder_1_out8),
    .out9(decoder_1_out9), .out10(decoder_1_out10), .out11(decoder_1_out11), .out12(decoder_1_out12),
    .out13(decoder_1_out13), .out14(decoder_1_out14), .out15(decoder_1_out15), .out16(decoder_1_out16),
    .out17(decoder_1_out17), .out18(decoder_1_out18), .out19(decoder_1_out19), .out20(decoder_1_out20),
    .out21(decoder_1_out21), .out22(decoder_1_out22), .out23(decoder_1_out23), .out24(decoder_1_out24),
    .out25(decoder_1_out25), .out26(decoder_1_out26), .out27(decoder_1_out27), .out28(decoder_1_out28),
    .out29(decoder_1_out29), .out30(decoder_1_out30), .out31(decoder_1_out31), .sel(Write_Register),
    .en(Write));  // open: out0
  Delayer1x32 delayer1x32_1 (.in(Write_Data), .out(delayer1x32_1_out));
  Register #(.width(32)) R1 (.D(delayer1x32_1_out), .en(decoder_1_out1), .Q(R1_q), .clk(clk), .clr(1'b0));
  Register #(.width(32)) R2 (.D(delayer1x32_1_out), .en(decoder_1_out2), .Q(R2_q), .clk(clk), .clr(1'b0));
  Register #(.width(32)) R3 (.D(delayer1x32_1_out), .en(decoder_1_out3), .Q(R3_q), .clk(clk), .clr(1'b0));
  Register #(.width(32)) R4 (.D(delayer1x32_1_out), .en(decoder_1_out4), .Q(R4_q), .clk(clk), .clr(1'b0));
  Register #(.width(32)) R5 (.D(delayer1x32_1_out), .en(decoder_1_out5), .Q(R5_q), .clk(clk), .clr(1'b0));
  Register #(.width(32)) R6 (.D(delayer1x32_1_out), .en(decoder_1_out6), .Q(R6_q), .clk(clk), .clr(1'b0));
  Register #(.width(32)) R7 (.D(delayer1x32_1_out), .en(decoder_1_out7), .Q(R7_q), .clk(clk), .clr(1'b0));
  Register #(.width(32)) R8 (.D(delayer1x32_1_out), .en(decoder_1_out8), .Q(R8_q), .clk(clk), .clr(1'b0));
  Register #(.width(32)) R9 (.D(delayer1x32_1_out), .en(decoder_1_out9), .Q(R9_q), .clk(clk), .clr(1'b0));
  Register #(.width(32)) R10 (.D(delayer1x32_1_out), .en(decoder_1_out10), .Q(R10_q), .clk(clk), .clr(1'b0));
  Register #(.width(32)) R11 (.D(delayer1x32_1_out), .en(decoder_1_out11), .Q(R11_q), .clk(clk), .clr(1'b0));
  Register #(.width(32)) R12 (.D(delayer1x32_1_out), .en(decoder_1_out12), .Q(R12_q), .clk(clk), .clr(1'b0));
  Register #(.width(32)) R13 (.D(delayer1x32_1_out), .en(decoder_1_out13), .Q(R13_q), .clk(clk), .clr(1'b0));
  Register #(.width(32)) R14 (.D(delayer1x32_1_out), .en(decoder_1_out14), .Q(R14_q), .clk(clk), .clr(1'b0));
  Register #(.width(32)) R15 (.D(delayer1x32_1_out), .en(decoder_1_out15), .Q(R15_q), .clk(clk), .clr(1'b0));
  Register #(.width(32)) R16 (.D(delayer1x32_1_out), .en(decoder_1_out16), .Q(R16_q), .clk(clk), .clr(1'b0));
  Register #(.width(32)) R17 (.D(delayer1x32_1_out), .en(decoder_1_out17), .Q(R17_q), .clk(clk), .clr(1'b0));
  Register #(.width(32)) R18 (.D(delayer1x32_1_out), .en(decoder_1_out18), .Q(R18_q), .clk(clk), .clr(1'b0));
  Register #(.width(32)) R19 (.D(delayer1x32_1_out), .en(decoder_1_out19), .Q(R19_q), .clk(clk), .clr(1'b0));
  Register #(.width(32)) R20 (.D(delayer1x32_1_out), .en(decoder_1_out20), .Q(R20_q), .clk(clk), .clr(1'b0));
  Register #(.width(32)) R21 (.D(delayer1x32_1_out), .en(decoder_1_out21), .Q(R21_q), .clk(clk), .clr(1'b0));
  Register #(.width(32)) R22 (.D(delayer1x32_1_out), .en(decoder_1_out22), .Q(R22_q), .clk(clk), .clr(1'b0));
  Register #(.width(32)) R23 (.D(delayer1x32_1_out), .en(decoder_1_out23), .Q(R23_q), .clk(clk), .clr(1'b0));
  Register #(.width(32)) R24 (.D(delayer1x32_1_out), .en(decoder_1_out24), .Q(R24_q), .clk(clk), .clr(1'b0));
  Register #(.width(32)) R25 (.D(delayer1x32_1_out), .en(decoder_1_out25), .Q(R25_q), .clk(clk), .clr(1'b0));
  Register #(.width(32)) R26 (.D(delayer1x32_1_out), .en(decoder_1_out26), .Q(R26_q), .clk(clk), .clr(1'b0));
  Register #(.width(32)) R27 (.D(delayer1x32_1_out), .en(decoder_1_out27), .Q(R27_q), .clk(clk), .clr(1'b0));
  Register #(.width(32)) R28 (.D(delayer1x32_1_out), .en(decoder_1_out28), .Q(R28_q), .clk(clk), .clr(1'b0));
  Register #(.width(32)) R29 (.D(delayer1x32_1_out), .en(decoder_1_out29), .Q(R29_q), .clk(clk), .clr(1'b0));
  Register #(.width(32)) R30 (.D(delayer1x32_1_out), .en(decoder_1_out30), .Q(R30_q), .clk(clk), .clr(1'b0));
  Register #(.width(32)) R31 (.D(delayer1x32_1_out), .en(decoder_1_out31), .Q(R31_q), .clk(clk), .clr(1'b0));
  Multiplexer #(.select(5), .width(32), .enable("false")) multiplexer_1 (
    .in0({32{1'b0}}), .in1(R1_q), .in2(R2_q), .in3(R3_q), .in4(R4_q), .in5(R5_q), .in6(R6_q), .in7(R7_q),
    .in8(R8_q), .in9(R9_q), .in10(R10_q), .in11(R11_q), .in12(R12_q), .in13(R13_q), .in14(R14_q),
    .in15(R15_q), .in16(R16_q), .in17(R17_q), .in18(R18_q), .in19(R19_q), .in20(R20_q), .in21(R21_q),
    .in22(R22_q), .in23(R23_q), .in24(R24_q), .in25(R25_q), .in26(R26_q), .in27(R27_q), .in28(R28_q),
    .in29(R29_q), .in30(R30_q), .in31(R31_q), .out(multiplexer_1_out), .sel(Read_Register_1));
  Multiplexer #(.select(5), .width(32), .enable("false")) multiplexer_2 (
    .in0({32{1'b0}}), .in1(R1_q), .in2(R2_q), .in3(R3_q), .in4(R4_q), .in5(R5_q), .in6(R6_q), .in7(R7_q),
    .in8(R8_q), .in9(R9_q), .in10(R10_q), .in11(R11_q), .in12(R12_q), .in13(R13_q), .in14(R14_q),
    .in15(R15_q), .in16(R16_q), .in17(R17_q), .in18(R18_q), .in19(R19_q), .in20(R20_q), .in21(R21_q),
    .in22(R22_q), .in23(R23_q), .in24(R24_q), .in25(R25_q), .in26(R26_q), .in27(R27_q), .in28(R28_q),
    .in29(R29_q), .in30(R30_q), .in31(R31_q), .out(multiplexer_2_out), .sel(Read_Register_2));
  Delayer1x32 delayer1x32_2 (.in(multiplexer_1_out), .out(Read_Data_1));
  Delayer1x32 delayer1x32_3 (.in(multiplexer_2_out), .out(Read_Data_2));
endmodule

module ALU (
  input  [3:0] Operation,
  input  [31:0] A,
  input  [31:0] B,
  output Z,
  output [31:0] Result
);

  wire [0:0] comparator_1_lt;
  wire [31:0] adder_1_out, and_1_out, multiplexer_1_out, multiplexer_2_out, multiplexer_3_out, not_1_out,
       not_2_out, or_1_out;

  assign not_1_out = ~A;  // NOT_Gate not_1, 32 bits wide
  assign not_2_out = ~B;  // NOT_Gate not_2, 32 bits wide
  Comparator #(.width(32)) comparator_1 (.a(A), .b(B), .lt(comparator_1_lt[0]));  // open: gt, eq
  Multiplexer #(.width(32), .enable("false")) multiplexer_1 (
    .in0(A), .in1(not_1_out), .out(multiplexer_1_out), .sel(Operation[3]));
  Multiplexer #(.width(32), .enable("false")) multiplexer_2 (
    .in0(B), .in1(not_2_out), .out(multiplexer_2_out), .sel(Operation[2]));
  assign and_1_out = multiplexer_1_out & multiplexer_2_out;  // AND_Gate and_1, 32 bits wide
  assign or_1_out = multiplexer_1_out | multiplexer_2_out;  // OR_Gate or_1, 32 bits wide
  Adder #(.width(32)) adder_1 (
    .a(multiplexer_1_out), .b(multiplexer_2_out), .out(adder_1_out), .cin(Operation[2]));  // open: cout
  Multiplexer #(.select(2), .width(32), .enable("false")) multiplexer_3 (
    .in0(and_1_out), .in1(or_1_out), .in2(adder_1_out), .in3({{31{1'b0}}, comparator_1_lt[0]}),
    .out(multiplexer_3_out), .sel(Operation[1:0]));
  nor nor_1 (Z, multiplexer_3_out[0], multiplexer_3_out[1], multiplexer_3_out[2], multiplexer_3_out[3], multiplexer_3_out[4], multiplexer_3_out[5], multiplexer_3_out[6], multiplexer_3_out[7], multiplexer_3_out[8], multiplexer_3_out[9], multiplexer_3_out[10], multiplexer_3_out[11], multiplexer_3_out[12], multiplexer_3_out[13], multiplexer_3_out[14], multiplexer_3_out[15], multiplexer_3_out[16], multiplexer_3_out[17], multiplexer_3_out[18], multiplexer_3_out[19], multiplexer_3_out[20], multiplexer_3_out[21], multiplexer_3_out[22], multiplexer_3_out[23], multiplexer_3_out[24], multiplexer_3_out[25], multiplexer_3_out[26], multiplexer_3_out[27], multiplexer_3_out[28], multiplexer_3_out[29], multiplexer_3_out[30], multiplexer_3_out[31]);
  Delayer2x32 delayer2x32_1 (.in(multiplexer_3_out), .out(Result));

  // Notes on the sheet:
  //   0001    OR
  //   Operation    Function
  //   0000    AND
  //   0010    add
  //   0110    subtract
  //   0111    set on less than
  //   1100    NOR
endmodule

module Control_ALU (
  input  [1:0] OpALU,
  input  [6:0] funct7,
  input  [2:0] funct3,
  input  op5,
  output [3:0] OUT
);

  wire and_1_out;
  wire [3:0] multiplexer_1_out, multiplexer_2_out;

  Multiplexer #(.width(4), .enable("false")) multiplexer_1 (
    .in0(4'b0010), .in1(4'b0110), .out(multiplexer_1_out), .sel(and_1_out));
  and and_1 (and_1_out, funct7[5], op5);
  Multiplexer #(.select(3), .width(4), .enable("false")) multiplexer_2 (
    .in0(multiplexer_1_out), .in2(4'b0111), .in6(4'b0001), .in7(4'b0000), .out(multiplexer_2_out),
    .sel(funct3));  // open: in1, in3, in4, in5
  Multiplexer #(.select(2), .width(4), .enable("false")) multiplexer_3 (
    .in0(4'b0010), .in1(4'b0110), .in2(multiplexer_2_out), .out(OUT), .sel(OpALU));  // open: in3

  // Notes on the sheet:
  //   OpALU    OUT
  //    00    add
  //    01    sub
  //    10    ALU y ALUI
endmodule

module Data_Memory_32 (
  input  Write,
  input  [31:0] Address,
  input  [31:0] Write_Data,
  input  clk,
  input  Read,
  output [31:0] Read_Data
);

  wire [9:0] bitselector_1_out;
  wire [31:0] delayer2x32_1_out, ram_1_data;

  BitSelector #(.width(32), .group(10)) bitselector_1 (.in(Address), .out(bitselector_1_out), .sel(2'b00));
  Delayer2x32 delayer2x32_1 (.in(Write_Data), .out(delayer2x32_1_out));
  RAM #(.dataWidth(32), .bus("separate"), .Datafile_on_reset("datamem.txt")) ram_1 (
    .addr(bitselector_1_out[9:2]), .din(delayer2x32_1_out), .data(ram_1_data), .str(Write), .sel(1'b1),
    .clk(clk), .ld(Read), .clr(1'b0));
  Delayer2x32 delayer2x32_2 (.in(ram_1_data), .out(Read_Data));

  // Notes on the sheet:
  //   Memoria de 32 bits direccionable a nivel de byte
  //   Tan solo implementadas las 256 primeras posiciones de 32 bits o 1024 bytes
endmodule

module Instruction_memory (
  input  [31:0] Read_address,
  output [31:0] Instruction
);

  wire [6:0] bitselector_1_out;
  wire [31:0] ram_1_data;

  BitSelector #(.width(30), .group(7)) bitselector_1 (.in(Read_address[31:2]), .out(bitselector_1_out), .sel(3'b000));
  RAM #(.addrWidth(7), .dataWidth(32), .bus("asynch"), .Datafile_on_reset("instmem.txt")) ram_1 (
    .addr(bitselector_1_out), .data(ram_1_data), .sel(1'b1), .ld(1'b1), .clr(1'b0));
  Delayer2x32 delayer2x32_1 (.in(ram_1_data), .out(Instruction));
endmodule

module PC (
  input  [31:0] IN,
  input  clk,
  output [31:0] PC
);

  Register #(.width(32)) u_PC (.D(IN), .en(1'b1), .Q(PC), .clk(clk));  // open: clr
endmodule

module Delayer2x32 (
  input  [31:0] in,
  output [31:0] out
);

  wire clock_1_out;
  wire [31:0] register_1_q;

  Clock clock_1 (.out(clock_1_out));
  Register #(.width(32)) register_1 (.D(in), .Q(register_1_q), .clk(clock_1_out));  // open: en, clr
  Register #(.width(32)) register_2 (.D(register_1_q), .Q(out), .clk(clock_1_out));  // open: en, clr
endmodule

module Delayer1x32 (
  input  [31:0] in,
  output [31:0] out
);

  wire clock_1_out;

  Clock clock_1 (.out(clock_1_out));
  Register #(.width(32)) register_1 (.D(in), .Q(out), .clk(clock_1_out));  // open: en, clr
endmodule

module Delayer2x1 (
  input  in,
  output out
);

  wire clock_1_out, register_1_q;

  Clock clock_1 (.out(clock_1_out));
  Register #(.width(1)) register_1 (.D(in), .Q(register_1_q), .clk(clock_1_out));  // open: en, clr
  Register #(.width(1)) register_2 (.D(register_1_q), .Q(out), .clk(clock_1_out));  // open: en, clr
endmodule

module ClockGen (
  input  halt,
  input  clkin,
  output clkout
);

  wire clock_1_out, d_ff_1_q, not_1_out;
  wire [31:0] adder_1_out, counter_1_q, counter_2_q, counter_3_q;

  Clock clock_1 (.out(clock_1_out));
  D_Flip_Flop d_ff_1 (.clk(halt), .D(halt), .Q(d_ff_1_q));  // open: Qn, preset, en, reset
  not not_1 (not_1_out, clkin);
  Counter #(.width(32), .max('hffffffff)) counter_1 (
    .Q(counter_1_q), .clk(clock_1_out));  // open: load, D, count, carry, clr
  Counter #(.width(32), .max('hffffffff), .trigger("falling")) counter_2 (
    .Q(counter_2_q), .clk(clock_1_out));  // open: load, D, count, carry, clr
  or or_1 (clkout, d_ff_1_q, not_1_out);
  Adder #(.width(32)) adder_1 (.a(counter_1_q), .b(counter_2_q), .out(adder_1_out));  // open: cin, cout
  // Probe on counter_3_q
  Counter #(.width(32), .max('hffffffff)) counter_3 (
    .Q(counter_3_q), .clk(clkout));  // open: load, D, count, carry, clr
  // Probe on adder_1_out
endmodule

module clock_divider (
  input  clk_in,
  output clk,
  output clk_2,
  output clk_4,
  output clk_8,
  output clk_16,
  output clk_32
);

  Counter #(.width(5), .max('h1f)) counter_1 (
    .Q({clk_32, clk_16, clk_8, clk_4, clk_2}), .clk(clk_in));  // open: load, D, count, carry, clr

  assign clk = clk_in;
endmodule
