// Logisim project SA28RISCV.circ as structural Verilog: 1 circuit, main circuit RISCV
module RISCV (
);

  wire clk, clock_1_out, HALT, JAL;
  wire [2:0] multiplexer_2_out;
  wire [3:0] control_alu_1_out;
  wire [4:0] RD;
  wire [6:0] OPCODE;
  wire [31:0] extender_1_out, Instruct_Memory, multiplexer_1_out, PC, PC_4, PC_JUMP;

  Clock #(.highDuration(2), .lowDuration(2)) clock_1 (.out(clock_1_out));
  // Probe on OPCODE
  Adder #(.width(32)) adder_1 (.a(32'h4), .b(PC), .out(PC_4));  // open: cin, cout
  PC pc_1 (.IN(multiplexer_1_out), .PC(PC), .clk(clk));
  Multiplexer #(.width(32), .enable("false")) multiplexer_1 (
    .in0(PC_4), .in1(PC_JUMP), .out(multiplexer_1_out), .sel(JAL));
  and and_1 (JAL, OPCODE[6], OPCODE[5], ~OPCODE[4], OPCODE[3], OPCODE[2], OPCODE[1], OPCODE[0]);  // AND_Gate
  ClockGen clockgen_1 (.halt(HALT), .clkin(clock_1_out), .clkout(clk));
  and and_2 (HALT, OPCODE[6], OPCODE[5], OPCODE[4], OPCODE[3], OPCODE[2], OPCODE[1], OPCODE[0]);
  Multiplexer #(.width(3), .enable("false")) multiplexer_2 (
    .in0(3'b000), .in1(3'b100), .out(multiplexer_2_out), .sel(JAL));
  Instruction_memory instruction_memory_1 (.Read_address(PC), .Instruction(Instruct_Memory));
  Extender extender_1 (.IB(Instruct_Memory), .OUT(extender_1_out), .TYPE(multiplexer_2_out));
  InstDecoder Inst_Decoder (
    .IB(Instruct_Memory), .IB6_0(OPCODE), .IB11_7(RD));  // open: IB19_15, IB24_20, IB14_12, IB31_25
  Adder #(.width(32)) adder_2 (.a(PC), .b(extender_1_out), .out(PC_JUMP));  // open: cin, cout
  Control_ALU control_alu_1 (.OUT(control_alu_1_out));  // open: OpALU, funct7, funct3, op5
  ALU alu_1 (.Operation(control_alu_1_out));  // open: A, B, Z, Result
  Register_file register_file_1 (
    .Write_Register(RD), .Write_Data(PC_4), .clk(clk), .Write(JAL));  // open: Read_Register_1, Read_Register_2, Read_Data_1, Read_Data_2
  Data_Memory_32 data_memory_32_1 (.clk(clk));  // open: Address, Write_Data, Read_Data, Write, Read
endmodule
