// Logisim project SA28RISCV.circ as structural Verilog: 1 circuit, main circuit RISCV
module RISCV (
);

  wire _001_out, _101_out, ALU, ALUI, and_1_out, and_2_out, and_3_out, and_4_out, and_17_out, and_19_out,
       and_21_out, and_23_out, AUIPC, B, BEQ, BGE, BLT, BNE, clk, clock_1_out, comparator_2_gt, CONTROL_PC,
       HALT, igual, JAL, JALR, LUI, LW, mayor, menor, OP5, or_2_out, or_3_out, or_4_out, or_5_out, or_6_out,
       or_7_out, RSUBLT, SI_RSUBLT, SLI, SLLI, SRLI, SW, zero;
  wire [1:1] or_8_out;
  wire [2:0] funct3, multiplexer_3_out, multiplexer_4_out, multiplexer_5_out, multiplexer_7_out, TYPE;
  wire [3:0] control_alu_1_out;
  wire [4:0] RD, RS1, RS2;
  wire [6:0] funct7, OPCODE;
  wire [31:0] ALU_A, ALU_B, ALURes, IMM, Instruct_Memory, MEM_DATA_OUT, multiplexer_1_out, multiplexer_2_out,
       multiplexer_8_out, multiplexer_9_out, multiplexer_10_out, multiplexer_11_out, PC, PC_4, PC_IMM,
       REG_DATA_IN, REG_DATA_OUT_2, RSUBLT_CALC;

  Clock #(.highDuration(10), .lowDuration(10)) clock_1 (.out(clock_1_out));
  Multiplexer #(.width(32), .enable("false")) multiplexer_1 (
    .in0(PC_4), .in1(ALURes), .out(multiplexer_1_out), .sel(JALR));
  or or_1 (CONTROL_PC, JAL, and_2_out, and_1_out, and_3_out, and_4_out);
  and and_1 (and_1_out, menor, BLT);
  and and_2 (and_2_out, zero, BEQ);
  and and_3 (and_3_out, ~zero, BNE);  // AND_Gate
  // Probe on {OPCODE[6], OP5, OPCODE[4:0]}
  ClockGen clockgen_1 (.halt(HALT), .clkin(clock_1_out), .clkout(clk));
  Adder #(.width(32)) adder_1 (.a(PC), .b(IMM), .out(PC_IMM));  // open: cin, cout
  Adder #(.width(32)) adder_2 (.a(32'h4), .b(PC), .out(PC_4));  // open: cin, cout
  Multiplexer #(.width(32), .enable("false")) multiplexer_2 (
    .in0(multiplexer_1_out), .in1(PC_IMM), .out(multiplexer_2_out), .sel(CONTROL_PC));
  PC pc_1 (.IN(multiplexer_2_out), .PC(PC), .clk(clk));
  and and_4 (and_4_out, or_2_out, BGE);
  or or_2 (or_2_out, mayor, igual);
  and and_5 (JAL, OPCODE[6], OP5, ~OPCODE[4], OPCODE[3], OPCODE[2], OPCODE[1], OPCODE[0]);  // AND_Gate
  and and_6 (HALT, OPCODE[6], OP5, OPCODE[4], OPCODE[3], OPCODE[2], OPCODE[1], OPCODE[0]);
  and and_7 (LW, ~OPCODE[6], ~OP5, ~OPCODE[4], ~OPCODE[3], ~OPCODE[2], OPCODE[1], OPCODE[0]);  // AND_Gate
  Instruction_memory instruction_memory_1 (.Read_address(PC), .Instruction(Instruct_Memory));
  and and_8 (SW, ~OPCODE[6], OP5, ~OPCODE[4], ~OPCODE[3], ~OPCODE[2], OPCODE[1], OPCODE[0]);  // AND_Gate
  // Probe on TYPE
  or or_3 (or_3_out, LW, ALUI);
  Multiplexer #(.width(3), .enable("false")) multiplexer_3 (
    .in0(multiplexer_4_out), .in1(3'b001), .out(multiplexer_3_out), .sel(SW));
  Multiplexer #(.width(3), .enable("false")) multiplexer_4 (
    .in0(multiplexer_5_out), .in1(3'b010), .out(multiplexer_4_out), .sel(B));
  Multiplexer #(.width(3), .enable("false")) multiplexer_5 (
    .in0(3'b000), .in1(3'b011), .out(multiplexer_5_out), .sel(or_4_out));
  or or_4 (or_4_out, AUIPC, LUI);
  InstDecoder Inst_Decoder (
    .IB(Instruct_Memory), .IB6_0({OPCODE[6], OP5, OPCODE[4:0]}), .IB11_7(RD), .IB19_15(RS1), .IB24_20(RS2),
    .IB14_12(funct3), .IB31_25(funct7));
  Extender extender_1 (.IB(Instruct_Memory), .OUT(IMM), .TYPE(TYPE));
  Multiplexer #(.width(3), .enable("false")) multiplexer_6 (
    .in0(multiplexer_7_out), .in1(3'b100), .out(TYPE), .sel(JAL));
  Multiplexer #(.width(3), .enable("false")) multiplexer_7 (
    .in0(multiplexer_3_out), .in1(3'b000), .out(multiplexer_7_out), .sel(or_3_out));
  and and_9 (ALU, ~OPCODE[6], OP5, OPCODE[4], ~OPCODE[3], ~OPCODE[2], OPCODE[1], OPCODE[0]);  // AND_Gate
  and and_10 (ALUI, ~OPCODE[6], ~OP5, OPCODE[4], ~OPCODE[3], ~OPCODE[2], OPCODE[1], OPCODE[0]);  // AND_Gate
  Multiplexer #(.width(32), .enable("false")) multiplexer_8 (
    .in0(PC_4), .in1(RSUBLT_CALC), .out(multiplexer_8_out), .sel(SI_RSUBLT));
  and and_11 (B, OPCODE[6], OP5, ~OPCODE[4], ~OPCODE[3], ~OPCODE[2], OPCODE[1], OPCODE[0]);  // AND_Gate
  Multiplexer #(.width(32), .enable("false")) multiplexer_9 (
    .in0(multiplexer_8_out), .in1(PC_IMM), .out(multiplexer_9_out), .sel(AUIPC));
  and and_12 (LUI, ~OPCODE[6], OP5, OPCODE[4], ~OPCODE[3], OPCODE[2], OPCODE[1], OPCODE[0]);  // AND_Gate
  or or_5 (or_5_out, SI_RSUBLT, JAL, LW, ALU, ALUI, LUI, AUIPC, JALR);
  Multiplexer #(.width(32), .enable("false")) multiplexer_10 (
    .in0(multiplexer_9_out), .in1(IMM), .out(multiplexer_10_out), .sel(LUI));
  Register_file register_file_1 (
    .Read_Register_1(RS1), .Read_Register_2(RS2), .Write_Register(RD), .Write_Data(REG_DATA_IN),
    .Read_Data_1(ALU_A), .Read_Data_2(REG_DATA_OUT_2), .clk(clk), .Write(or_5_out));
  and and_13 (AUIPC, ~OPCODE[6], ~OP5, OPCODE[4], ~OPCODE[3], OPCODE[2], OPCODE[1], OPCODE[0]);  // AND_Gate
  or or_6 (or_6_out, ALU, ALUI);
  and and_14 (JALR, OPCODE[6], OP5, ~OPCODE[4], ~OPCODE[3], OPCODE[2], OPCODE[1], OPCODE[0]);  // AND_Gate
  Multiplexer #(.width(32), .enable("false")) multiplexer_11 (
    .in0(multiplexer_10_out), .in1(ALURes), .out(multiplexer_11_out), .sel(or_6_out));
  Multiplexer #(.width(32), .enable("false")) multiplexer_12 (
    .in0(multiplexer_11_out), .in1(MEM_DATA_OUT), .out(REG_DATA_IN), .sel(LW));
  and and_15 (SLI, ~OPCODE[6], ~OP5, OPCODE[4], ~OPCODE[3], ~OPCODE[2], OPCODE[1], OPCODE[0]);  // AND_Gate
  and and_16 (RSUBLT, OPCODE[6], ~OP5, OPCODE[4], ~OPCODE[3], OPCODE[2], ~OPCODE[1], OPCODE[0]);  // AND_Gate
  Multiplexer #(.width(32), .enable("false")) multiplexer_13 (
    .in0(IMM), .in1(REG_DATA_OUT_2), .out(ALU_B), .sel(or_7_out));
  or or_7 (or_7_out, B, ALU);
  or or_8 (or_8_out[1], ALUI, ALU);
  Control_ALU control_alu_1 (
    .OpALU({or_8_out[1], B}), .funct7(funct7), .OUT(control_alu_1_out), .funct3(funct3), .op5(OP5));
  and and_17 (and_17_out, ~funct3[2], ~funct3[1], ~funct3[0]);  // AND_Gate
  and and_18 (BEQ, B, and_17_out);
  // Probe on {or_8_out[1], B}
  // Probe on control_alu_1_out
  ALU alu_1 (.A(ALU_A), .B(ALU_B), .Z(zero), .Result(ALURes), .Operation(control_alu_1_out));
  and and_19 (and_19_out, ~funct3[2], ~funct3[1], funct3[0]);  // AND_Gate
  and and_20 (BNE, and_19_out, B);
  Data_Memory_32 data_memory_32_1 (
    .Address(ALURes), .Write_Data(REG_DATA_OUT_2), .Read_Data(MEM_DATA_OUT), .Write(SW), .clk(clk), .Read(LW));
  and and_21 (and_21_out, funct3[2], ~funct3[1], ~funct3[0]);  // AND_Gate
  and and_22 (BLT, and_21_out, B);
  Comparator #(.width(32)) comparator_1 (.a(ALU_A), .b(REG_DATA_OUT_2), .gt(mayor), .eq(igual), .lt(menor));
  and and_23 (and_23_out, funct3[2], ~funct3[1], funct3[0]);  // AND_Gate
  and and_24 (BGE, and_23_out, B);
  and _001 (_001_out, ~funct3[2], ~funct3[1], funct3[0]);  // AND_Gate
  and and_25 (SLLI, SLI, _001_out);
  and _101 (_101_out, funct3[2], ~funct3[1], funct3[0]);  // AND_Gate
  and and_26 (SRLI, _101_out, SLI);
  Comparator #(.width(32)) comparator_2 (.a(ALU_A), .b(REG_DATA_OUT_2), .gt(comparator_2_gt));  // open: eq, lt
  Subtractor #(.width(32)) subtractor_1 (.a(ALU_A), .b(REG_DATA_OUT_2), .out(RSUBLT_CALC));  // open: bin, bout
  and and_27 (SI_RSUBLT, comparator_2_gt, RSUBLT);

  // Other names for the same wires on the sheet: OPCODE[5] = OP5; REG_DATA_OUT_1[31:0] = ALU_A

  // Notes on the sheet:
  //   MODULOS DE PC
  //   MODULO OPCODE
  //   1101111
  //   1111111
  //   0000011
  //   0100011
  //   MODULO MEMORIA DE INSTRUCCION
  //   MODULO EXTENDEDOR
  //   0110011
  //   0010011
  //   1100011
  //   0110111
  //   MODULO REGISTROS
  //   0010111
  //   1100111
  //   0010011
  //   1010101
  //   MODULO ALU
  //   MODULO DATA MEMORY
  //   MODULO SALTOS CONDICIONALES
  //   MODULO EXTRA
  //   MODULO DESPLAZAMIENTO INMEDIATO SLI
endmodule
